# Fritzing sketch TestBox (saved by Fritzing 0.7.10b)
breadboards: 1

parts:
  Teensy1 = Teensy++ 2.0
  R1 = Resistor [tolerance=±5% resistance=220 package=THT]
  R2 = Resistor [tolerance=±5% resistance=220 package=THT]
  R3 = Resistor [tolerance=±5% resistance=220 package=THT]
  LED9 = LED - 3mm [color="Red (635nm)" package="3 mm [THT]"]
  LED8 = LED - 3mm [color="Red (635nm)" package="3 mm [THT]"]
  LED7 = LED - 3mm [color="Red (635nm)" package="3 mm [THT]"]
  LED1 = LED - 3mm [color="Green (555nm)" package="3 mm [THT]"]
  LED5 = LED - 3mm [color="Green (555nm)" package="3 mm [THT]"]
  LED6 = LED - 3mm [color="Green (555nm)" package="3 mm [THT]"]
  R4 = Resistor [tolerance=±5% resistance=220 package=THT]
  R5 = Resistor [tolerance=±5% resistance=220 package=THT]
  R6 = Resistor [tolerance=±5% resistance=220 package=THT]
  S1 = Toggle Switch [package=THT]
  LCD1 = LCD screen
  R7 = Trimmer Potentiometer [maximum_resistance=10kΩ package=THT]
  RE1 = Rotary Encoder [package=THT]
  RE2 = Rotary Encoder [package=THT]
  S2 = Pushbutton [package=THT]
  S3 = Pushbutton [package=THT]

nets:
  N1: Teensy1.GND#0, LED9.cathode, LED8.cathode, LED7.cathode, LED1.cathode, LED5.cathode, LED6.cathode, S1.COM, LCD1.VSS, LCD1.LED-, R7.leg2, RE1.EncoderPinC, RE2.EncoderPinC, S2.leg0, S3.leg0
  N2: Teensy1.B7, LCD1.RS
  N3: Teensy1.D0, LCD1.R/W
  N4: Teensy1.D1, LCD1.E, LCD1.DB0
  N5: Teensy1.D2, LCD1.DB4
  N6: Teensy1.D3, LCD1.DB5
  N7: Teensy1.D4, LCD1.DB6
  N8: Teensy1.D5, LCD1.DB7
  N9: Teensy1.D7, RE1.EncoderPinA
  N10: Teensy1.E0, RE1.EncoderPinB
  N11: Teensy1.E1, RE2.EncoderPinA
  N12: Teensy1.C0, RE2.EncoderPinB
  N13: Teensy1.C1, S2.leg1
  N14: Teensy1.C2, R2.Pin_0
  N15: Teensy1.C3, R1.Pin_0
  N16: Teensy1.C4, R3.Pin_0
  N17: Teensy1.C5, R4.Pin_0
  N18: Teensy1.C6, R5.Pin_0
  N19: Teensy1.C7, R6.Pin_0
  N20: Teensy1.F7, S1.L1
  N21: Teensy1.B0, S3.leg1
  N22: Teensy1.B4, LCD1.LED+
  VCC: Teensy1.VCC, LCD1.VDD, R7.leg1
  N23: R1.Pin_1, LED7.anode
  N24: R2.Pin_1, LED9.anode
  N25: R3.Pin_1, LED8.anode
  N26: LED1.anode, R5.Pin_1
  N27: LED5.anode, R4.Pin_1
  N28: LED6.anode, R6.Pin_1
  N29: LCD1.V0, R7.wiper
